// Logisim project branch_comp.circ as structural Verilog: 1 circuit, main circuit branch_comp
module branch_comp (
  input  [31:0] rs1,
  input  [31:0] rs2,
  input  BrUn,
  output BrEq,
  output BrLt
);

  wire eq, lt, uneq, unlt;

  Comparator #(.width(32)) comparator_1 (.a(rs1), .b(rs2), .eq(eq), .lt(lt));  // open: gt
  Comparator #(.mode("unsigned"), .width(32)) comparator_2 (.a(rs1), .b(rs2), .eq(uneq), .lt(unlt));  // open: gt
  Multiplexer multiplexer_1 (.in0(eq), .in1(uneq), .out(BrEq), .sel(BrUn));
  Multiplexer multiplexer_2 (.in0(lt), .in1(unlt), .out(BrLt), .sel(BrUn));

  // Notes on the sheet:
  //   INPUTS to your circuit
  //   DON'T CHANGE THE LOCATIONS OF THE INPUTS AND OUTPUTS!
  //   OUTPUT from your circuit
endmodule
