// Logisim project cpu.circ as structural Verilog: 1 circuit, main circuit cpu
module cpu (
  input  clk,
  input  [31:0] INSTRUCTION,
  input  [31:0] READ_DATA,
  output [31:0] WRITE_ADDRESS,
  output [31:0] PROGRAM_COUNTER,
  output [31:0] ra,
  output [31:0] sp,
  output [31:0] t0,
  output [31:0] t1,
  output [31:0] t2,
  output [31:0] s0,
  output [31:0] s1,
  output [31:0] a0,
  output [31:0] tohost,
  output [3:0] WRITE_ENABLE,
  output [31:0] WRITE_DATA
);

  wire ASel, BrEq, BrLt, BrUn, BSel, CSRSel, CSRWen, MemRW, PCSel, RegWEn;
  wire [1:0] WBSel;
  wire [2:0] ImmSel;
  wire [3:0] ALUSel;
  wire [31:0] adder_1_out, adder_2_out, bit_extender_1_out, dataD, ex_inst, ex_pc, imm, multiplexer_1_out,
       multiplexer_2_out, multiplexer_3_out, multiplexer_4_out, multiplexer_5_out, rs1;

  Multiplexer #(.width(32)) multiplexer_1 (
    .in0(adder_1_out), .in1(WRITE_ADDRESS), .out(multiplexer_1_out), .sel(PCSel));
  Adder #(.width(32)) adder_1 (.a(PROGRAM_COUNTER), .b(32'h4), .out(adder_1_out));  // open: cin, cout
  Register #(.width(32)) PC (.D(multiplexer_1_out), .clk(clk), .Q(PROGRAM_COUNTER));  // open: en, clr
  Register #(.width(32)) inst_reg (.D(multiplexer_2_out), .clk(clk), .Q(ex_inst));  // open: en, clr
  Multiplexer #(.width(32)) multiplexer_2 (.in0(INSTRUCTION), .in1({32{1'b0}}), .out(multiplexer_2_out), .sel(PCSel));
  Register #(.width(32)) u_ex_pc (.D(PROGRAM_COUNTER), .clk(clk), .Q(ex_pc));  // open: en, clr
  control_logic control_logic_1 (
    .inst(ex_inst), .BrEq(BrEq), .BrLt(BrLt), .CSRWen(CSRWen), .PCSel(PCSel), .RegWEn(RegWEn),
    .ImmSel(ImmSel), .BrUn(BrUn), .ASel(ASel), .BSel(BSel), .ALUSel(ALUSel), .MemRW(MemRW), .WBSel(WBSel),
    .CSRSel(CSRSel));
  imm_gen imm_gen_1 (.inst(ex_inst), .ImmSel(ImmSel), .imm(imm));
  regfile regfile_1 (
    .rs1(ex_inst[19:15]), .rs2(ex_inst[24:20]), .rd(ex_inst[11:7]), .Write_Data(dataD), .RegWEn(RegWEn),
    .clk(clk), .ra(ra), .sp(sp), .t0(t0), .t1(t1), .t2(t2), .s0(s0), .s1(s1), .a0(a0), .Read_Data_1(rs1),
    .Read_Data_2(WRITE_DATA));
  branch_comp branch_comp_1 (.rs1(rs1), .rs2(WRITE_DATA), .BrUn(BrUn), .BrEq(BrEq), .BrLt(BrLt));
  assign bit_extender_1_out = {{27{1'b0}}, ex_inst[19:15]};  // Bit_Extender bit_extender_1
  Multiplexer #(.width(32)) multiplexer_3 (.in0(rs1), .in1(bit_extender_1_out), .out(multiplexer_3_out), .sel(CSRSel));
  Multiplexer #(.width(32)) multiplexer_4 (.in0(rs1), .in1(ex_pc), .out(multiplexer_4_out), .sel(ASel));
  Multiplexer #(.width(32)) multiplexer_5 (.in0(WRITE_DATA), .in1(imm), .out(multiplexer_5_out), .sel(BSel));
  alu alu_1 (.A(multiplexer_4_out), .B(multiplexer_5_out), .ALUSel(ALUSel), .Result(WRITE_ADDRESS));
  csr csr_1 (.CSR_address(12'h51e), .CSR_din(multiplexer_3_out), .CSR_WE(CSRWen), .clk(clk), .tohost(tohost));
  Adder #(.width(32)) adder_2 (.a(ex_pc), .b(32'h4), .out(adder_2_out));  // open: cin, cout
  assign WRITE_ENABLE = {{3{MemRW}}, MemRW};  // Bit_Extender bit_extender_2
  Multiplexer #(.select(2), .width(32)) multiplexer_6 (
    .in0(READ_DATA), .in1(WRITE_ADDRESS), .in2(adder_2_out), .out(dataD), .sel(WBSel));  // open: in3

  // Other names for the same wires on the sheet: ALUOutput[31:0] = WRITE_ADDRESS; dataB[31:0] = READ_DATA;
  //   opcode[6:0] = ex_inst[6:0]; rd[4:0] = ex_inst[11:7]; funct3[2:0] = ex_inst[14:12];
  //   targetrs1[4:0] = ex_inst[19:15]; targetrs2[4:0] = ex_inst[24:20]; funct7[6:0] = ex_inst[31:25];
  //   rs2[31:0] = WRITE_DATA

  // Notes on the sheet:
  //   Output to IMEM
  //   IMEM (do **NOT** move this)
  //   Inputs from IMEM
  //   It is OK to move the PC, RegFile, ALU, MEM, Branch Comp, Imm Gen, and Control Logic to wherever is most convenient for you when constructing your CPU, and to delete this text
  //   Inputs/Outputs for testing. Do **NOT** move these.
  //   Outputs To DMEM
  //   DMEM (do **NOT** move this)
  //   Inputs From DMEM
endmodule
