// Logisim project imm_gen.circ as structural Verilog: 1 circuit, main circuit imm_gen
module imm_gen (
  input  [31:0] inst,
  input  [2:0] ImmSel,
  output [31:0] imm
);

  wire [31:0] Itype0, SBtype2, Stype1, UJtype2, UJtype4;

  assign Itype0 = {{20{inst[31]}}, inst[31:20]};  // Bit_Extender bit_extender_1
  assign Stype1 = {{20{inst[31]}}, {inst[31:25], inst[11:7]}};  // Bit_Extender bit_extender_2
  assign SBtype2 = {{19{inst[31]}}, {inst[31], inst[7], inst[30:25], inst[11:8], 1'b0}};  // Bit_Extender bit_extender_3
  assign UJtype4 = {{11{inst[31]}}, {inst[31], inst[19:12], inst[20], inst[30:21], 1'b0}};  // Bit_Extender bit_extender_4
  Multiplexer #(.select(3), .width(32)) multiplexer_1 (
    .in0(Itype0), .in1(Stype1), .in2(SBtype2), .in3({inst[31:12], {12{1'b0}}}), .in4(UJtype2), .out(imm),
    .sel(ImmSel));  // open: in5, in6, in7

  // Other names for the same wires on the sheet: Utype3[31:12] = inst[31:12]

  // Notes on the sheet:
  //   INPUTS to your circuit
  //   DON'T CHANGE THE LOCATIONS OF THE INPUTS AND OUTPUTS!
  //   OUTPUT from your circuit
endmodule
