// Logisim project regfile - 副本.circ as structural Verilog: 1 circuit, main circuit regfile
module regfile (
  input  [4:0] rs1,
  input  [4:0] rs2,
  input  [4:0] rd,
  input  [31:0] Write_Data,
  input  RegWEn,
  input  clk,
  output [31:0] ra,
  output [31:0] sp,
  output [31:0] t0,
  output [31:0] t1,
  output [31:0] t2,
  output [31:0] s0,
  output [31:0] s1,
  output [31:0] a0,
  output [31:0] Read_Data_1,
  output [31:0] Read_Data_2
);

  wire demultiplexer_1_out1, demultiplexer_1_out2, demultiplexer_1_out3, demultiplexer_1_out4,
       demultiplexer_1_out5, demultiplexer_1_out6, demultiplexer_1_out7, demultiplexer_1_out8,
       demultiplexer_1_out9, demultiplexer_1_out10, demultiplexer_1_out11;
  wire [31:0] x1, x2, x3, x4, x5, x6, x7, x8, x9, x10, x11;

  Demultiplexer #(.select(5)) demultiplexer_1 (
    .out1(demultiplexer_1_out1), .out2(demultiplexer_1_out2), .out3(demultiplexer_1_out3),
    .out4(demultiplexer_1_out4), .out5(demultiplexer_1_out5), .out6(demultiplexer_1_out6),
    .out7(demultiplexer_1_out7), .out8(demultiplexer_1_out8), .out9(demultiplexer_1_out9),
    .out10(demultiplexer_1_out10), .out11(demultiplexer_1_out11), .in(RegWEn), .sel(rd));  // open: out0, out12, out13, out14, out15, out16, out17, out18, out19, out20, out21, out22, out23, out24, out25, out26, out27, out28, out29, out30, out31
  Register #(.width(32)) u_x1 (.D(Write_Data), .en(demultiplexer_1_out1), .clk(clk), .Q(x1));  // open: clr
  Register #(.width(32)) u_x2 (.D(Write_Data), .en(demultiplexer_1_out2), .clk(clk), .Q(x2));  // open: clr
  Register #(.width(32)) u_x3 (.D(Write_Data), .en(demultiplexer_1_out3), .clk(clk), .Q(x3));  // open: clr
  Register #(.width(32)) u_x4 (.D(Write_Data), .en(demultiplexer_1_out4), .clk(clk), .Q(x4));  // open: clr
  Register #(.width(32)) u_x5 (.D(Write_Data), .en(demultiplexer_1_out5), .clk(clk), .Q(x5));  // open: clr
  Register #(.width(32)) u_x6 (.D(Write_Data), .en(demultiplexer_1_out6), .clk(clk), .Q(x6));  // open: clr
  Register #(.width(32)) u_x7 (.D(Write_Data), .en(demultiplexer_1_out7), .clk(clk), .Q(x7));  // open: clr
  Register #(.width(32)) u_x8 (.D(Write_Data), .en(demultiplexer_1_out8), .clk(clk), .Q(x8));  // open: clr
  Register #(.width(32)) u_x9 (.D(Write_Data), .en(demultiplexer_1_out9), .clk(clk), .Q(x9));  // open: clr
  Register #(.width(32)) u_x10 (.D(Write_Data), .en(demultiplexer_1_out10), .clk(clk), .Q(x10));  // open: clr
  Register #(.width(32)) u_x11 (.D(Write_Data), .en(demultiplexer_1_out11), .clk(clk), .Q(x11));  // open: clr
  Multiplexer #(.select(5), .width(32)) multiplexer_1 (
    .in0({32{1'b0}}), .in1(x1), .in2(x2), .in3(x3), .in4(x4), .in5(x5), .in6(x6), .in7(x7), .in8(x8),
    .in9(x9), .in10(x10), .in11(x11), .out(Read_Data_1), .sel(rs1));  // open: in12, in13, in14, in15, in16, in17, in18, in19, in20, in21, in22, in23, in24, in25, in26, in27, in28, in29, in30, in31

  // Other names for the same wires on the sheet: read_data1[31:0] = Read_Data_1; read_data2[31:0] = Read_Data_2;
  //   read_reg1[4:0] = rs1; read_reg2[4:0] = rs2; write_en = RegWEn; write_reg[4:0] = rd

  // Notes on the sheet:
  //   INPUTS to your circuit
  //   DON'T CHANGE THE LOCATIONS OF THE INPUTS AND OUTPUTS!
  //   These are DEBUG/TEST outputs from your circuit.
  //   OUTPUTS from your circuit
endmodule
